// Logisim project army_hard_coding_competition.circ as structural Verilog
module _5_bit_adder (
  input  V,
  input  W,
  input  X,
  input  Y,
  input  Z,
  output Sum,
  output Cout
);

  wire and_1_out, and_2_out, and_3_out, and_4_out, and_5_out;

  and and_1 (and_1_out, V, W);
  and and_2 (and_2_out, W, X);
  and and_3 (and_3_out, X, Y);
  and and_4 (and_4_out, Y, Z);
  and and_5 (and_5_out, Z, V);
  ExactlyOne xor_1 (.out(Sum), .in0(Z), .in1(Y), .in2(X), .in3(W), .in4(V));
  or or_1 (Cout, and_1_out, and_2_out, and_3_out, and_4_out, and_5_out);
endmodule
